// Logisim project ATM_SCHEMA_FINALA.circ as structural Verilog: 1 circuit, main circuit main
module main (
  input  [1:0] Adresa,
  input  OP0,
  input  OP1,
  input  Exit
);

  wire _10_out, _20_out, _50_out, _100_out, clock_1_out, Clr_out, Dec_out, identificator_card_1_pin_corect,
       Inc_out, main_1_out_3, main_2_out_3, main_3_out_3, main_4_out_3, main_5_out_3, main_6_out_3,
       main_7_out_3, main_8_out_3, main_9_out_3, main_10_out_3, main_16_depunere,
       main_16_enable_algoritm_depunere, main_16_enable_algoritm_retragere, main_16_led_chitanta,
       main_16_led_fail, main_16_led_retragere_succes, main_16_led_succes, main_16_schimba_pin,
       main_17_validare, main_19_depunere_posibila, main_20_s0, main_20_s1, main_20_s2, main_20_s3,
       main_20_s4, main_20_s5, main_21_retragere_posibila, N_out, OK_out, or_1_out, or_2_out, P_out;
  wire [2:0] main_16_sold, main_17_selected;
  wire [3:0] bit_extender_7_out, bit_extender_8_out, bit_extender_9_out, bit_extender_10_out,
       bit_extender_11_out, bit_extender_12_out, main_11_io0, main_11_io1, main_11_io2, main_11_io3,
       main_11_io4, main_11_io5, main_12_n0, main_12_n1, main_12_n2, main_12_n3, main_12_n4, main_12_n5,
       main_17_a0, main_17_a1, main_17_a2, main_17_a3, main_17_a4, main_17_a5, main_20_d0, main_20_d0_2,
       main_20_d1, main_20_d1_2, main_20_d2, main_20_d2_2, main_20_d3, main_20_d3_2, main_20_d4,
       main_20_d4_2, main_20_d5, multiplexer_8_out, multiplexer_9_out, multiplexer_10_out,
       multiplexer_11_out, multiplexer_12_out, multiplexer_13_out;
  wire [4:0] main_15_stare_curenta;
  wire [7:4] main_20_d5_2;
  wire [15:0] bit_extender_1_out, bit_extender_2_out, bit_extender_3_out, bit_extender_4_out,
       bit_extender_5_out, bit_extender_6_out, main_13_suma_out, main_14_disp10, main_14_disp20,
       main_14_disp50, main_14_disp100, main_14_disp200, main_14_disp500, main_18_zecimal,
       main_19_suma_update, main_19_update5, main_19_update10, main_19_update20, main_19_update50,
       main_19_update100, main_19_update500, main_21_suma_update, main_21_u5, main_21_u10, main_21_u20,
       main_21_u50, main_21_u100, main_21_u500, main_21_update5, main_21_update10, main_21_update20,
       main_21_update50, main_21_update100, main_21_update500, multiplexer_1_out, multiplexer_2_out,
       multiplexer_3_out, multiplexer_4_out, multiplexer_5_out, multiplexer_6_out, multiplexer_7_out;

  or or_1 (or_1_out, main_16_depunere, main_16_sold[1]);
  Clock clock_1 (.out(clock_1_out));
  Button Clr (.out(Clr_out));
  Button _10 (.out(_10_out));
  Button _20 (.out(_20_out));
  Button _50 (.out(_50_out));
  Button _100 (.out(_100_out));
  Button Inc (.out(Inc_out));
  Button Dec (.out(Dec_out));
  Button N (.out(N_out));
  Button P (.out(P_out));
  Button OK (.out(OK_out));
  Multiplexer #(.width(16), .enable("false")) multiplexer_1 (
    .in0(main_19_suma_update), .in1(main_21_suma_update), .out(multiplexer_1_out), .sel(main_16_sold[1]));
  Multiplexer #(.width(16), .enable("false")) multiplexer_2 (
    .in0(main_19_update500), .in1(main_21_update500), .out(multiplexer_2_out), .sel(main_16_sold[1]));
  Multiplexer #(.width(16), .enable("false")) multiplexer_3 (
    .in0(main_19_update100), .in1(main_21_update100), .out(multiplexer_3_out), .sel(main_16_sold[1]));
  Multiplexer #(.width(16), .enable("false")) multiplexer_4 (
    .in0(main_19_update50), .in1(main_21_update50), .out(multiplexer_4_out), .sel(main_16_sold[1]));
  Multiplexer #(.width(16), .enable("false")) multiplexer_5 (
    .in0(main_19_update20), .in1(main_21_update20), .out(multiplexer_5_out), .sel(main_16_sold[1]));
  Multiplexer #(.width(16), .enable("false")) multiplexer_6 (
    .in0(main_19_update10), .in1(main_21_update10), .out(multiplexer_6_out), .sel(main_16_sold[1]));
  Multiplexer #(.width(16), .enable("false")) multiplexer_7 (
    .in0(main_19_update5), .in1(main_21_update5), .out(multiplexer_7_out), .sel(main_16_sold[1]));
  deboncer_main main_1 (.in_1(Clr_out), .Clk(clock_1_out), .out_3(main_1_out_3));
  deboncer_main main_2 (.in_1(_10_out), .Clk(clock_1_out), .out_3(main_2_out_3));
  deboncer_main main_3 (.in_1(_20_out), .Clk(clock_1_out), .out_3(main_3_out_3));
  deboncer_main main_4 (.in_1(_50_out), .Clk(clock_1_out), .out_3(main_4_out_3));
  deboncer_main main_5 (.in_1(_100_out), .Clk(clock_1_out), .out_3(main_5_out_3));
  deboncer_main main_6 (.in_1(Inc_out), .Clk(clock_1_out), .out_3(main_6_out_3));
  deboncer_main main_7 (.in_1(Dec_out), .Clk(clock_1_out), .out_3(main_7_out_3));
  deboncer_main main_8 (.in_1(N_out), .Clk(clock_1_out), .out_3(main_8_out_3));
  deboncer_main main_9 (.in_1(P_out), .Clk(clock_1_out), .out_3(main_9_out_3));
  deboncer_main main_10 (.in_1(OK_out), .Clk(clock_1_out), .out_3(main_10_out_3));
  incarcare_suma_predefinita_main main_11 (
    ._10(main_2_out_3), ._20(main_3_out_3), ._50(main_4_out_3), ._100(main_5_out_3),
    .io_load_enable(main_16_sold[2]), .io0(main_11_io0), .io1(main_11_io1), .io2(main_11_io2),
    .io3(main_11_io3), .io4(main_11_io4), .io5(main_11_io5));
  dec_to_io_main main_12 (
    .Zecimal(main_13_suma_out), .N3(main_12_n3), .N2(main_12_n2), .N1(main_12_n1), .N0(main_12_n0),
    .N4(main_12_n4), .N5(main_12_n5));
  memorie_suma_main main_13 (
    .Adress(Adresa), .Suma_out(main_13_suma_out), .Data(multiplexer_1_out), .Wesuma(or_1_out),
    .Clock(clock_1_out));  // open: Clear
  memorie_bancnote_main main_14 (
    .WE_BANCNOTE(or_1_out), .Clock(clock_1_out), .Up100(multiplexer_4_out), .Up50(multiplexer_5_out),
    .Up20(multiplexer_6_out), .Up10(multiplexer_7_out), .Disp100(main_14_disp100), .Disp50(main_14_disp50),
    .Disp20(main_14_disp20), .Disp10(main_14_disp10), .Up200(multiplexer_3_out), .Disp200(main_14_disp200),
    .Up500(multiplexer_2_out), .Disp500(main_14_disp500));
  organigrama_main main_15 (
    .VALIDARE(main_17_validare), .PIN_CORECT(identificator_card_1_pin_corect), .IESIRE_CONT(Exit),
    .OP_1(OP1), .OP_0(OP0), .RETRAGERE_POSIBILA(main_21_retragere_posibila),
    .DEPUNERE_POSIBILA(main_19_depunere_posibila), .CLK(clock_1_out), .RESET(1'b0),
    .STARE_CURENTA(main_15_stare_curenta));  // open: STAREA_VIITOARE
  Multiplexer #(.select(3), .width(4), .disabled(0), .enable("false")) multiplexer_8 (
    .in1(main_12_n0), .in2(bit_extender_12_out), .in4(main_11_io0), .out(multiplexer_8_out),
    .sel(main_16_sold));  // open: in0, in3, in5, in6, in7
  Multiplexer #(.select(3), .width(4), .enable("false")) multiplexer_9 (
    .in1(main_12_n1), .in2(bit_extender_11_out), .in4(main_11_io1), .out(multiplexer_9_out),
    .sel(main_16_sold));  // open: in0, in3, in5, in6, in7
  Multiplexer #(.select(3), .width(4), .enable("false")) multiplexer_10 (
    .in1(main_12_n2), .in2(bit_extender_10_out), .in4(main_11_io2), .out(multiplexer_10_out),
    .sel(main_16_sold));  // open: in0, in3, in5, in6, in7
  Multiplexer #(.select(3), .width(4), .enable("false")) multiplexer_11 (
    .in1(main_12_n3), .in2(bit_extender_9_out), .in4(main_11_io3), .out(multiplexer_11_out),
    .sel(main_16_sold));  // open: in0, in3, in5, in6, in7
  Multiplexer #(.select(3), .width(4), .enable("false")) multiplexer_12 (
    .in1(main_12_n4), .in2(bit_extender_8_out), .in4(main_11_io4), .out(multiplexer_12_out),
    .sel(main_16_sold));  // open: in0, in3, in5, in6, in7
  Multiplexer #(.select(3), .width(4), .enable("false")) multiplexer_13 (
    .in1(main_12_n5), .in2(bit_extender_7_out), .in4(main_11_io5), .out(multiplexer_13_out),
    .sel(main_16_sold));  // open: in0, in3, in5, in6, in7
  iesiri_organigrama_main main_16 (
    .STARE(main_15_stare_curenta), .SOLD(main_16_sold[0]), .LED_SUCCES(main_16_led_succes),
    .ENABLE_ALGORITM_RETRAGERE(main_16_enable_algoritm_retragere), .RETRAGERE(main_16_sold[1]),
    .LED_RETRAGERE_SUCCES(main_16_led_retragere_succes), .LED_FAIL(main_16_led_fail),
    .SCHIMBA_PIN(main_16_schimba_pin), .DEPUNERE(main_16_depunere),
    .ENABLE_ALGORITM_DEPUNERE(main_16_enable_algoritm_depunere), .LED_CHITANTA(main_16_led_chitanta));  // open: ENABLE_COMPARATOR_PIN
  _7_Segment_Display u_7_segment_display_1 (
    .g(main_20_d5_2[6]), .f(main_20_d5_2[5]), .a(main_20_d5[0]), .b(main_20_d5[1]), .e(main_20_d5_2[4]),
    .d(main_20_d5[3]), .c(main_20_d5[2]), .dp(main_20_s5));
  LED CHITANTA (.in(main_16_led_chitanta));
  LED Fail (.in(main_16_led_fail));
  or or_2 (or_2_out, main_16_sold[0], main_16_sold[1], main_16_sold[2]);
  LED Ok_2 (.in(main_16_led_succes));
  LED RETRAGERE (.in(main_16_led_retragere_succes));
  _7_Segment_Display u_7_segment_display_2 (
    .g(main_20_d4_2[2]), .f(main_20_d4_2[1]), .a(main_20_d4[0]), .b(main_20_d4[1]), .e(main_20_d4_2[0]),
    .d(main_20_d4[3]), .c(main_20_d4[2]), .dp(main_20_s4));
  assign bit_extender_1_out = {{12{1'b0}}, main_17_a0};  // Bit_Extender bit_extender_1
  _7_Segment_Display u_7_segment_display_3 (
    .g(main_20_d3_2[2]), .f(main_20_d3_2[1]), .a(main_20_d3[0]), .b(main_20_d3[1]), .e(main_20_d3_2[0]),
    .d(main_20_d3[3]), .c(main_20_d3[2]), .dp(main_20_s3));
  assign bit_extender_2_out = {{12{1'b0}}, main_17_a1};  // Bit_Extender bit_extender_2
  memorie_io_main main_17 (
    .Increment(main_6_out_3), .Decrement(main_7_out_3), .Confirm(main_10_out_3), .Load(or_2_out),
    .Clear(main_1_out_3), .Data0(multiplexer_8_out), .Data1(multiplexer_9_out), .Data2(multiplexer_10_out),
    .Data3(multiplexer_11_out), .Next(main_8_out_3), .Prev(main_9_out_3), .Validare(main_17_validare),
    .a0(main_17_a0), .a1(main_17_a1), .a2(main_17_a2), .a3(main_17_a3), .selected(main_17_selected),
    .a4(main_17_a4), .a5(main_17_a5), .Data4(multiplexer_12_out), .Data5(multiplexer_13_out),
    .Clock(clock_1_out));
  _7_Segment_Display u_7_segment_display_4 (
    .g(main_20_d2_2[2]), .f(main_20_d2_2[1]), .a(main_20_d2[0]), .b(main_20_d2[1]), .e(main_20_d2_2[0]),
    .d(main_20_d2[3]), .c(main_20_d2[2]), .dp(main_20_s2));
  assign bit_extender_3_out = {{12{1'b0}}, main_17_a2};  // Bit_Extender bit_extender_3
  assign bit_extender_4_out = {{12{1'b0}}, main_17_a3};  // Bit_Extender bit_extender_4
  _7_Segment_Display u_7_segment_display_5 (
    .g(main_20_d1_2[2]), .f(main_20_d1_2[1]), .a(main_20_d1[0]), .b(main_20_d1[1]), .e(main_20_d1_2[0]),
    .d(main_20_d1[3]), .c(main_20_d1[2]), .dp(main_20_s1));
  assign bit_extender_5_out = {{12{1'b0}}, main_17_a4};  // Bit_Extender bit_extender_5
  _7_Segment_Display u_7_segment_display_6 (
    .g(main_20_d0_2[2]), .f(main_20_d0_2[1]), .a(main_20_d0[0]), .b(main_20_d0[1]), .e(main_20_d0_2[0]),
    .d(main_20_d0[3]), .c(main_20_d0[2]), .dp(main_20_s0));
  assign bit_extender_6_out = {{12{1'b0}}, main_17_a5};  // Bit_Extender bit_extender_6
  io_to_dec_main main_18 (
    .N0(main_17_a0), .N1(main_17_a1), .N2(main_17_a2), .N3(main_17_a3), .Zecimal(main_18_zecimal),
    .N4(main_17_a4), .N5(main_17_a5));
  algoritm_depunere_main main_19 (
    .Suma_Cont(main_13_suma_out), .Dep50(bit_extender_4_out), .Disp50(main_14_disp100),
    .Dep20(bit_extender_3_out), .Disp20(main_14_disp50), .Dep10(bit_extender_2_out), .Disp10(main_14_disp20),
    .Dep5(bit_extender_1_out), .Disp5(main_14_disp10),
    .Enable_Algoritm_Depunere(main_16_enable_algoritm_depunere), .Update50(main_19_update50),
    .Update20(main_19_update20), .Update10(main_19_update10), .Suma_Update(main_19_suma_update),
    .Depunere_Posibila(main_19_depunere_posibila), .Update5(main_19_update5), .Dep100(bit_extender_5_out),
    .Update100(main_19_update100), .Disp100(main_14_disp200), .Dep500(bit_extender_6_out),
    .Update500(main_19_update500), .Disp500(main_14_disp500));
  afisare_main main_20 (
    .a0(main_17_a0), .a1(main_17_a1), .a2(main_17_a2), .a3(main_17_a3), .Selected(main_17_selected),
    .d0({main_20_d0_2, main_20_d0}), .s0(main_20_s0), .d1({main_20_d1_2, main_20_d1}), .s1(main_20_s1),
    .d2({main_20_d2_2, main_20_d2}), .s2(main_20_s2), .d3({main_20_d3_2, main_20_d3}), .s3(main_20_s3),
    .a4(main_17_a4), .d4({main_20_d4_2, main_20_d4}), .s4(main_20_s4), .a5(main_17_a5),
    .d5({main_20_d5_2, main_20_d5}), .s5(main_20_s5));
  algoritm_retragere_main main_21 (
    .Suma_Cont(main_13_suma_out), .Suma_Retragere(main_18_zecimal), .D50(main_14_disp100),
    .D20(main_14_disp50), .enable(main_16_enable_algoritm_retragere), .D10(main_14_disp20),
    .D5(main_14_disp10), .U50(main_21_u50), .Update50(main_21_update50), .Suma_Update(main_21_suma_update),
    .U20(main_21_u20), .Update20(main_21_update20), .U10(main_21_u10),
    .Retragere_Posibila(main_21_retragere_posibila), .Update10(main_21_update10), .U5(main_21_u5),
    .Update5(main_21_update5), .U100(main_21_u100), .Update100(main_21_update100), .D100(main_14_disp200),
    .U500(main_21_u500), .Update500(main_21_update500), .D500(main_14_disp500));
  IDENTIFICATOR_CARD identificator_card_1 (
    .IN_PIN(main_18_zecimal), .PIN_NOU(main_18_zecimal), .VERIFY_WRITE_PIN(main_16_schimba_pin),
    .IN_ADR(Adresa), .PIN_CORECT(identificator_card_1_pin_corect), .CLK(clock_1_out));
  Bit_Extender #(.in_width(16), .out_width(4)) bit_extender_7 (.in(main_21_u500), .out(bit_extender_7_out));
  Bit_Extender #(.in_width(16), .out_width(4)) bit_extender_8 (.in(main_21_u100), .out(bit_extender_8_out));
  Bit_Extender #(.in_width(16), .out_width(4)) bit_extender_9 (.in(main_21_u50), .out(bit_extender_9_out));
  Bit_Extender #(.in_width(16), .out_width(4)) bit_extender_10 (.in(main_21_u20), .out(bit_extender_10_out));
  Bit_Extender #(.in_width(16), .out_width(4)) bit_extender_11 (.in(main_21_u10), .out(bit_extender_11_out));
  Bit_Extender #(.in_width(16), .out_width(4)) bit_extender_12 (.in(main_21_u5), .out(bit_extender_12_out));
endmodule
