// Logisim project afisare.circ as structural Verilog: 1 circuit, main circuit main
module main (
  input  [3:0] a0,
  input  [3:0] a1,
  input  [3:0] a2,
  input  [3:0] a3,
  input  [3:0] a4,
  input  [3:0] a5,
  input  [2:0] Selected,
  output [7:0] d0,
  output s0,
  output [7:0] d1,
  output s1,
  output [7:0] d2,
  output s2,
  output [7:0] d3,
  output s3,
  output [7:0] d4,
  output s4,
  output [7:0] d5,
  output s5
);

  wire demultiplexer_1_out0, demultiplexer_1_out1, demultiplexer_1_out2, demultiplexer_1_out3,
       demultiplexer_1_out4, demultiplexer_1_out5;

  Demultiplexer #(.select(3), .enable("false")) demultiplexer_1 (
    .out0(demultiplexer_1_out0), .out1(demultiplexer_1_out1), .out2(demultiplexer_1_out2),
    .out3(demultiplexer_1_out3), .out4(demultiplexer_1_out4), .out5(demultiplexer_1_out5), .in(1'b1),
    .sel(Selected));  // open: out6, out7
  dcd_7seg_main main_1 (.Value(a0), .Sel(demultiplexer_1_out0), .Out(d0), .Select(s0));
  dcd_7seg_main main_2 (.Value(a1), .Sel(demultiplexer_1_out1), .Out(d1), .Select(s1));
  dcd_7seg_main main_3 (.Value(a2), .Sel(demultiplexer_1_out2), .Out(d2), .Select(s2));
  dcd_7seg_main main_4 (.Value(a3), .Sel(demultiplexer_1_out3), .Out(d3), .Select(s3));
  dcd_7seg_main main_5 (.Value(a4), .Sel(demultiplexer_1_out4), .Out(d4), .Select(s4));
  dcd_7seg_main main_6 (.Value(a5), .Sel(demultiplexer_1_out5), .Out(d5), .Select(s5));
endmodule
