// Logisim project algoritm_depunere.circ as structural Verilog: 1 circuit, main circuit main
module main (
  input  [15:0] Suma_Cont,
  input  [15:0] Dep500,
  input  [15:0] Disp500,
  input  [15:0] Dep100,
  input  [15:0] Disp100,
  input  [15:0] Dep50,
  input  [15:0] Disp50,
  input  [15:0] Dep20,
  input  [15:0] Disp20,
  input  [15:0] Dep10,
  input  [15:0] Disp10,
  input  [15:0] Dep5,
  input  [15:0] Disp5,
  input  Enable_Algoritm_Depunere,
  output [15:0] Update500,
  output [15:0] Update100,
  output [15:0] Update50,
  output [15:0] Update20,
  output [15:0] Update10,
  output [15:0] Suma_Update,
  output Depunere_Posibila,
  output [15:0] Update5
);

  wire comparator_1_lt, or_1_out;
  wire [15:0] adder_7_out, adder_8_out, adder_9_out, adder_10_out, adder_11_out, multiplier_1_out,
       multiplier_2_out, multiplier_3_out, multiplier_4_out, multiplier_5_out, multiplier_6_out;

  Multiplier #(.width(16)) multiplier_1 (.a(Dep500), .b(16'h1f4), .out(multiplier_1_out));  // open: cin, cout
  Adder #(.width(16)) adder_1 (.a(Dep500), .b(Disp500), .out(Update500));  // open: cin, cout
  Multiplier #(.width(16)) multiplier_2 (.a(Dep100), .b(16'h64), .out(multiplier_2_out));  // open: cin, cout
  Adder #(.width(16)) adder_2 (.a(Dep100), .b(Disp100), .out(Update100));  // open: cin, cout
  Multiplier #(.width(16)) multiplier_3 (.a(Dep50), .b(16'h32), .out(multiplier_3_out));  // open: cin, cout
  Adder #(.width(16)) adder_3 (.a(Dep50), .b(Disp50), .out(Update50));  // open: cin, cout
  Multiplier #(.width(16)) multiplier_4 (.a(Dep20), .b(16'h14), .out(multiplier_4_out));  // open: cin, cout
  Adder #(.width(16)) adder_4 (.a(Dep20), .b(Disp20), .out(Update20));  // open: cin, cout
  Multiplier #(.width(16)) multiplier_5 (.a(Dep10), .b(16'ha), .out(multiplier_5_out));  // open: cin, cout
  Adder #(.width(16)) adder_5 (.a(Dep10), .b(Disp10), .out(Update10));  // open: cin, cout
  Multiplier #(.width(16)) multiplier_6 (.a(Dep5), .b(16'h5), .out(multiplier_6_out));  // open: cin, cout
  Adder #(.width(16)) adder_6 (.a(Dep5), .b(Disp5), .out(Update5));  // open: cin, cout
  Adder #(.width(16)) adder_7 (.a(multiplier_1_out), .b(multiplier_2_out), .out(adder_7_out));  // open: cin, cout
  Adder #(.width(16)) adder_8 (.a(adder_7_out), .b(multiplier_3_out), .out(adder_8_out));  // open: cin, cout
  Adder #(.width(16)) adder_9 (.a(adder_8_out), .b(multiplier_4_out), .out(adder_9_out));  // open: cin, cout
  Adder #(.width(16)) adder_10 (.a(adder_9_out), .b(multiplier_5_out), .out(adder_10_out));  // open: cin, cout
  Adder #(.width(16)) adder_11 (.a(adder_10_out), .b(multiplier_6_out), .out(adder_11_out));  // open: cin, cout
  Adder #(.width(16)) adder_12 (.a(Suma_Cont), .b(adder_11_out), .out(Suma_Update));  // open: cin, cout
  Comparator #(.width(16), .mode("unsigned")) comparator_1 (
    .a(adder_11_out), .b(16'h3e8), .lt(comparator_1_lt));  // open: gt, eq
  or or_1 (or_1_out, 1'b1, Enable_Algoritm_Depunere);
  and and_1 (Depunere_Posibila, comparator_1_lt, or_1_out);
endmodule
