// Logisim project algoritm_retragere.circ as structural Verilog: 1 circuit, main circuit main
module main (
  input  [15:0] Suma_Cont,
  input  [15:0] Suma_Retragere,
  input  [15:0] D500,
  input  [15:0] D100,
  input  [15:0] D50,
  input  [15:0] D20,
  input  enable,
  input  [15:0] D10,
  input  [15:0] D5,
  output [15:0] U500,
  output [15:0] Update500,
  output [15:0] U100,
  output [15:0] Update100,
  output [15:0] U50,
  output [15:0] Update50,
  output [15:0] Suma_Update,
  output [15:0] U20,
  output [15:0] Update20,
  output [15:0] U10,
  output Retragere_Posibila,
  output [15:0] Update10,
  output [15:0] U5,
  output [15:0] Update5
);

  wire comparator_1_gt, comparator_2_gt, comparator_3_gt, comparator_4_gt, comparator_5_gt, comparator_6_gt,
       comparator_7_eq, comparator_7_gt, comparator_8_eq, comparator_9_lt, or_1_out, or_2_out;
  wire [15:0] divider_1_out, divider_2_out, divider_3_out, divider_4_out, divider_5_out, divider_6_out,
       multiplier_1_out, multiplier_2_out, multiplier_3_out, multiplier_4_out, multiplier_5_out,
       multiplier_6_out, subtractor_7_out, subtractor_8_out, subtractor_9_out, subtractor_10_out,
       subtractor_11_out, subtractor_12_out;

  Divider #(.width(16)) divider_1 (.a(Suma_Retragere), .b(16'h1f4), .out(divider_1_out));  // open: upper, rem
  Divider #(.width(16)) divider_2 (.a(subtractor_7_out), .b(16'h64), .out(divider_2_out));  // open: upper, rem
  Divider #(.width(16)) divider_3 (.a(subtractor_8_out), .b(16'h32), .out(divider_3_out));  // open: upper, rem
  Divider #(.width(16)) divider_4 (.a(subtractor_9_out), .b(16'h14), .out(divider_4_out));  // open: upper, rem
  Divider #(.width(16)) divider_5 (.a(subtractor_10_out), .b(16'ha), .out(divider_5_out));  // open: upper, rem
  Divider #(.width(16)) divider_6 (.a(subtractor_11_out), .b(16'h5), .out(divider_6_out));  // open: upper, rem
  Comparator #(.width(16), .mode("unsigned")) comparator_1 (
    .a(divider_1_out), .b(D500), .gt(comparator_1_gt));  // open: eq, lt
  Comparator #(.width(16), .mode("unsigned")) comparator_2 (
    .a(divider_2_out), .b(D100), .gt(comparator_2_gt));  // open: eq, lt
  Comparator #(.width(16), .mode("unsigned")) comparator_3 (
    .a(divider_3_out), .b(D50), .gt(comparator_3_gt));  // open: eq, lt
  Comparator #(.width(16), .mode("unsigned")) comparator_4 (
    .a(divider_4_out), .b(D20), .gt(comparator_4_gt));  // open: eq, lt
  Comparator #(.width(16), .mode("unsigned")) comparator_5 (
    .a(divider_5_out), .b(D10), .gt(comparator_5_gt));  // open: eq, lt
  Comparator #(.width(16), .mode("unsigned")) comparator_6 (
    .a(divider_6_out), .b(D5), .gt(comparator_6_gt));  // open: eq, lt
  Multiplexer #(.width(16), .enable("false")) multiplexer_1 (
    .in0(divider_1_out), .in1(D500), .out(U500), .sel(comparator_1_gt));
  Multiplexer #(.width(16), .enable("false")) multiplexer_2 (
    .in0(divider_2_out), .in1(D100), .out(U100), .sel(comparator_2_gt));
  Multiplexer #(.width(16), .enable("false")) multiplexer_3 (
    .in0(divider_3_out), .in1(D50), .out(U50), .sel(comparator_3_gt));
  Multiplexer #(.width(16), .enable("false")) multiplexer_4 (
    .in0(divider_4_out), .in1(D20), .out(U20), .sel(comparator_4_gt));
  Multiplexer #(.width(16), .enable("false")) multiplexer_5 (
    .in0(divider_5_out), .in1(D10), .out(U10), .sel(comparator_5_gt));
  Multiplexer #(.width(16), .enable("false")) multiplexer_6 (
    .in0(divider_6_out), .in1(D5), .out(U5), .sel(comparator_6_gt));
  Subtractor #(.width(16)) subtractor_1 (.a(D500), .b(U500), .out(Update500));  // open: bin, bout
  Multiplier #(.width(16)) multiplier_1 (.a(U500), .b(16'h1f4), .out(multiplier_1_out));  // open: cin, cout
  Subtractor #(.width(16)) subtractor_2 (.a(D100), .b(U100), .out(Update100));  // open: bin, bout
  Multiplier #(.width(16)) multiplier_2 (.a(U100), .b(16'h64), .out(multiplier_2_out));  // open: cin, cout
  Subtractor #(.width(16)) subtractor_3 (.a(D50), .b(U50), .out(Update50));  // open: bin, bout
  Multiplier #(.width(16)) multiplier_3 (.a(U50), .b(16'h32), .out(multiplier_3_out));  // open: cin, cout
  Subtractor #(.width(16)) subtractor_4 (.a(D20), .b(U20), .out(Update20));  // open: bin, bout
  Multiplier #(.width(16)) multiplier_4 (.a(U20), .b(16'h14), .out(multiplier_4_out));  // open: cin, cout
  Subtractor #(.width(16)) subtractor_5 (.a(D10), .b(U10), .out(Update10));  // open: bin, bout
  Multiplier #(.width(16)) multiplier_5 (.a(U10), .b(16'ha), .out(multiplier_5_out));  // open: cin, cout
  Subtractor #(.width(16)) subtractor_6 (.a(D5), .b(U5), .out(Update5));  // open: bin, bout
  Multiplier #(.width(16)) multiplier_6 (.a(U5), .b(16'h5), .out(multiplier_6_out));  // open: cin, cout
  Subtractor #(.width(16)) subtractor_7 (
    .a(Suma_Retragere), .b(multiplier_1_out), .out(subtractor_7_out));  // open: bin, bout
  Subtractor #(.width(16)) subtractor_8 (
    .a(subtractor_7_out), .b(multiplier_2_out), .out(subtractor_8_out));  // open: bin, bout
  Subtractor #(.width(16)) subtractor_9 (
    .a(subtractor_8_out), .b(multiplier_3_out), .out(subtractor_9_out));  // open: bin, bout
  Subtractor #(.width(16)) subtractor_10 (
    .a(subtractor_9_out), .b(multiplier_4_out), .out(subtractor_10_out));  // open: bin, bout
  Subtractor #(.width(16)) subtractor_11 (
    .a(subtractor_10_out), .b(multiplier_5_out), .out(subtractor_11_out));  // open: bin, bout
  Subtractor #(.width(16)) subtractor_12 (
    .a(subtractor_11_out), .b(multiplier_6_out), .out(subtractor_12_out));  // open: bin, bout
  Subtractor #(.width(16)) subtractor_13 (.a(Suma_Cont), .b(Suma_Retragere), .out(Suma_Update));  // open: bin, bout
  Comparator #(.width(16), .mode("unsigned")) comparator_7 (
    .a(Suma_Cont), .b(Suma_Retragere), .gt(comparator_7_gt), .eq(comparator_7_eq));  // open: lt
  Comparator #(.width(16), .mode("unsigned")) comparator_8 (
    .a(subtractor_12_out), .b({16{1'b0}}), .eq(comparator_8_eq));  // open: gt, lt
  or or_1 (or_1_out, enable, 1'b1);
  or or_2 (or_2_out, comparator_7_gt, comparator_7_eq);
  and and_1 (Retragere_Posibila, comparator_9_lt, or_2_out, comparator_8_eq, or_1_out);
  Comparator #(.width(16), .mode("unsigned")) comparator_9 (
    .a(Suma_Retragere), .b(16'h3e8), .lt(comparator_9_lt));  // open: gt, eq
endmodule
