// Logisim project dcd_7seg.circ as structural Verilog: 1 circuit, main circuit main
module main (
  input  [3:0] Value,
  input  Sel,
  output [7:0] Out,
  output Select
);

  ROM #(.addrWidth(4)) rom_1 (.addr(Value), .data(Out), .sel(1'b1));

  assign Select = Sel;

  // Notes on the sheet:
  //   contents of rom_1 (hex, n*v repeats v):
  //   3f 6 5b 4f 66 6d 7d 7 7f 6f 77 7c 39 5e 79 71
endmodule
