// Logisim project deboncer.circ as structural Verilog: 2 circuits, main circuit main
module main (
  input  in_1,
  input  Clk,
  output out_3
);

  wire d_ff_1_q, d_ff_2_qn;

  D_Flip_Flop d_ff_1 (.clk(Clk), .D(in_1), .Q(d_ff_1_q), .en(1'b1));  // open: Qn, preset, reset
  D_Flip_Flop d_ff_2 (.clk(Clk), .D(d_ff_1_q), .Qn(d_ff_2_qn), .en(1'b1));  // open: Q, preset, reset
  and and_1 (out_3, d_ff_2_qn, d_ff_1_q);
endmodule

module freq_divider (
  output out_1
);

  wire clock_1_out, d_ff_1_qn, d_ff_2_qn, d_ff_3_qn, d_ff_4_qn, d_ff_5_qn, d_ff_6_qn, d_ff_7_qn, d_ff_8_qn;

  Clock clock_1 (.out(clock_1_out));
  D_Flip_Flop d_ff_1 (.clk(clock_1_out), .D(d_ff_1_qn), .Qn(d_ff_1_qn), .en(1'b1));  // open: Q, preset, reset
  D_Flip_Flop d_ff_2 (.clk(d_ff_8_qn), .D(d_ff_2_qn), .Qn(d_ff_2_qn), .en(1'b1));  // open: Q, preset, reset
  D_Flip_Flop d_ff_3 (.clk(d_ff_1_qn), .D(d_ff_3_qn), .Qn(d_ff_3_qn), .en(1'b1));  // open: Q, preset, reset
  D_Flip_Flop d_ff_4 (.clk(d_ff_2_qn), .D(d_ff_4_qn), .Qn(d_ff_4_qn), .en(1'b1));  // open: Q, preset, reset
  D_Flip_Flop d_ff_5 (.clk(d_ff_3_qn), .D(d_ff_5_qn), .Qn(d_ff_5_qn), .en(1'b1));  // open: Q, preset, reset
  D_Flip_Flop d_ff_6 (.clk(d_ff_4_qn), .D(d_ff_6_qn), .Q(out_1), .Qn(d_ff_6_qn), .en(1'b1));  // open: preset, reset
  D_Flip_Flop d_ff_7 (.clk(d_ff_5_qn), .D(d_ff_7_qn), .Qn(d_ff_7_qn), .en(1'b1));  // open: Q, preset, reset
  D_Flip_Flop d_ff_8 (.clk(d_ff_7_qn), .D(d_ff_8_qn), .Qn(d_ff_8_qn), .en(1'b1));  // open: Q, preset, reset
endmodule
