// Logisim project dec_to_io.circ as structural Verilog: 1 circuit, main circuit main
module main (
  input  [15:0] Zecimal,
  output [3:0] N5,
  output [3:0] N4,
  output [3:0] N3,
  output [3:0] N2,
  output [3:0] N1,
  output [3:0] N0
);

  wire [15:0] divider_1_rem, divider_2_out, divider_2_rem, divider_3_out, divider_3_rem, divider_4_out,
       divider_4_rem, divider_5_out, divider_5_rem, divider_6_out, divider_6_rem;

  Divider #(.width(16)) divider_1 (.a(divider_2_out), .b(16'ha), .rem(divider_1_rem));  // open: out, upper
  Bit_Extender #(.in_width(16), .out_width(4)) bit_extender_1 (.in(divider_1_rem), .out(N5));
  Divider #(.width(16)) divider_2 (
    .a(divider_3_out), .b(16'ha), .out(divider_2_out), .rem(divider_2_rem));  // open: upper
  Bit_Extender #(.in_width(16), .out_width(4)) bit_extender_2 (.in(divider_2_rem), .out(N4));
  Divider #(.width(16)) divider_3 (
    .a(divider_4_out), .b(16'ha), .out(divider_3_out), .rem(divider_3_rem));  // open: upper
  Bit_Extender #(.in_width(16), .out_width(4)) bit_extender_3 (.in(divider_3_rem), .out(N3));
  Divider #(.width(16)) divider_4 (
    .a(divider_5_out), .b(16'ha), .out(divider_4_out), .rem(divider_4_rem));  // open: upper
  Bit_Extender #(.in_width(16), .out_width(4)) bit_extender_4 (.in(divider_4_rem), .out(N2));
  Divider #(.width(16)) divider_5 (
    .a(divider_6_out), .b(16'ha), .out(divider_5_out), .rem(divider_5_rem));  // open: upper
  Bit_Extender #(.in_width(16), .out_width(4)) bit_extender_5 (.in(divider_5_rem), .out(N1));
  Divider #(.width(16)) divider_6 (.a(Zecimal), .b(16'ha), .out(divider_6_out), .rem(divider_6_rem));  // open: upper
  Bit_Extender #(.in_width(16), .out_width(4)) bit_extender_6 (.in(divider_6_rem), .out(N0));
endmodule
