// Logisim project identificator_card.circ as structural Verilog: 1 circuit, main circuit IDENTIFICATOR_CARD
module IDENTIFICATOR_CARD (
  input  [15:0] IN_PIN,
  input  [15:0] PIN_NOU,
  input  VERIFY_WRITE_PIN,
  input  [1:0] IN_ADR,
  input  CLK,
  output PIN_CORECT
);

  wire comparator_1_eq, nand_1_out;
  wire [15:0] EEPROM_PIN_mem_pin;

  MEM_pin EEPROM_PIN (
    .PIN_NOU(PIN_NOU), .WE(VERIFY_WRITE_PIN), .IN_ADR(IN_ADR), .CLK(CLK), .CS(1'b1),
    .MEM_PIN(EEPROM_PIN_mem_pin));
  nand nand_1 (nand_1_out, VERIFY_WRITE_PIN, 1'b0);
  Comparator #(.width(16)) comparator_1 (.a(IN_PIN), .b(EEPROM_PIN_mem_pin), .eq(comparator_1_eq));  // open: gt, lt
  and and_1 (PIN_CORECT, comparator_1_eq, nand_1_out);
endmodule
