// Logisim project iesiri_organigrama.circ as structural Verilog: 1 circuit, main circuit main
module main (
  input  [4:0] STARE,
  output ENABLE_COMPARATOR_PIN,
  output SOLD,
  output LED_SUCCES,
  output ENABLE_ALGORITM_RETRAGERE,
  output RETRAGERE,
  output LED_RETRAGERE_SUCCES,
  output LED_FAIL,
  output SCHIMBA_PIN,
  output DEPUNERE,
  output ENABLE_ALGORITM_DEPUNERE,
  output LED_CHITANTA
);

  wire demultiplexer_1_out11, demultiplexer_1_out15, demultiplexer_1_out16, demultiplexer_1_out18;

  Demultiplexer #(.select(5)) demultiplexer_1 (
    .out1(ENABLE_COMPARATOR_PIN), .out7(LED_CHITANTA), .out8(ENABLE_ALGORITM_RETRAGERE), .out10(RETRAGERE),
    .out11(demultiplexer_1_out11), .out12(LED_RETRAGERE_SUCCES), .out13(ENABLE_ALGORITM_DEPUNERE),
    .out14(DEPUNERE), .out15(demultiplexer_1_out15), .out16(demultiplexer_1_out16), .out17(SCHIMBA_PIN),
    .out18(demultiplexer_1_out18), .in(1'b1), .sel(STARE), .en(1'b1));  // open: out0, out2, out3, out4, out5, out6, out9, out19, out20, out21, out22, out23, out24, out25, out26, out27, out28, out29, out30, out31
  or or_1 (LED_SUCCES, demultiplexer_1_out18, LED_CHITANTA, demultiplexer_1_out16);
  or or_2 (LED_FAIL, demultiplexer_1_out11, demultiplexer_1_out15);

  assign SOLD = LED_CHITANTA;

  // Notes on the sheet:
  //   DEPUNERE: pull=down
  //   SCHIMBA_PIN: pull=down
  //   LED_RETRAGERE_SUCCES: pull=down
  //   LED_SUCCES: pull=down
  //   ENABLE_ALGORITM_RETRAGERE: pull=down
  //   STARE: pull=down
  //   LED_FAIL: pull=down
  //   ENABLE_ALGORITM_DEPUNERE: pull=down
  //   ENABLE_COMPARATOR_PIN: pull=down
  //   SOLD: pull=down
  //   RETRAGERE: pull=down
endmodule
