// Logisim project incarcare_suma_predefinita.circ as structural Verilog: 1 circuit, main circuit main
module main (
  input  _10,
  input  _20,
  input  _50,
  input  _100,
  output io_load_enable,
  output [3:0] io0,
  output [3:0] io1,
  output [3:0] io2,
  output [3:0] io3,
  output [3:0] io4,
  output [3:0] io5
);

  Multiplexer #(.select(4), .width(4), .disabled(0), .enable("false")) multiplexer_1 (
    .in0(4'b0000), .in1(4'b0001), .in2(4'b0010), .in3(4'b0000), .in4(4'b0101), .in5(4'b0000), .in6(4'b0000),
    .in7(4'b0000), .in8(4'b0000), .in9(4'b0000), .in10(4'b0000), .in11(4'b0000), .in12(4'b0000),
    .in13(4'b0000), .in14(4'b0000), .in15(4'b0000), .out(io1), .sel({_100, _50, _20, _10}));
  Multiplexer #(.select(4), .width(4), .disabled(0), .enable("false")) multiplexer_2 (
    .in0(4'b0000), .in1(4'b0000), .in2(4'b0000), .in3(4'b0000), .in4(4'b0000), .in5(4'b0000), .in6(4'b0000),
    .in7(4'b0000), .in8(4'b0001), .in9(4'b0000), .in10(4'b0000), .in11(4'b0000), .in12(4'b0000),
    .in13(4'b0000), .in14(4'b0000), .in15(4'b0000), .out(io2), .sel({_100, _50, _20, _10}));
  or or_1 (io_load_enable, _10, _20, _50, _100);

  assign io0 = 4'b0000;
  assign io3 = 4'b0000;
  assign io4 = 4'b0000;
  assign io5 = 4'b0000;
endmodule
