// Logisim project io_test.circ as structural Verilog: 1 circuit, main circuit main
module main (
  input  Afisare_Sold,
  input  [1:0] in_2,
  output [3:0] out_3,
  output [3:0] out_4,
  output [3:0] out_5,
  output [3:0] out_6
);

  wire button_1_out, main_1_out_3, main_2_out_3, main_3_out_3, main_4_out_3, main_5_p3, main_6_out_3,
       main_7_out_3, main_8_out_3, main_9_out_3, main_11_p5, main_16_p12, or_1_out;
  wire [3:0] bit_extender_1_out, bit_extender_2_out, bit_extender_3_out, bit_extender_4_out, main_11_p6,
       main_11_p7, main_11_p8, main_11_p9, main_12_n0, main_12_n1, main_12_n2, main_12_n3, main_13_p5,
       main_13_p6, main_13_p7, main_13_p8, multiplexer_1_out, multiplexer_2_out, multiplexer_3_out,
       multiplexer_4_out, multiplexer_5_out, multiplexer_6_out, multiplexer_7_out, multiplexer_8_out;
  wire [9:0] bit_extender_5_out, bit_extender_6_out, bit_extender_7_out, bit_extender_8_out,
       bit_extender_9_out, bit_extender_11_out, bit_extender_12_out, bit_extender_13_out, main_14_p1,
       main_17_p10, main_17_p11, main_17_p12, main_17_p13;
  wire [13:0] main_15_p1;
  wire [15:0] main_10_p3;

  Button button_1 (.out(button_1_out));
  Button button_2 (.out(button_1_out));
  Button button_3 (.out(button_1_out));
  Button button_4 (.out(button_1_out));
  Button button_5 (.out(button_1_out));
  Button button_6 (.out(button_1_out));
  Button button_7 (.out(button_1_out));
  Button button_8 (.out(button_1_out));
  Button button_9 (.out(button_1_out));
  Bit_Extender #(.in_width(10), .out_width(4)) bit_extender_1 (.in(main_17_p10), .out(bit_extender_1_out));
  Bit_Extender #(.in_width(10), .out_width(4)) bit_extender_2 (.in(main_17_p11), .out(bit_extender_2_out));
  Bit_Extender #(.in_width(10), .out_width(4)) bit_extender_3 (.in(main_17_p12), .out(bit_extender_3_out));
  Bit_Extender #(.in_width(10), .out_width(4)) bit_extender_4 (.in(main_17_p13), .out(bit_extender_4_out));
  deboncer_main main_1 (.in_1(button_1_out), .Clk(button_1_out), .out_3(main_1_out_3));
  deboncer_main main_2 (.in_1(button_1_out), .Clk(button_1_out), .out_3(main_2_out_3));
  deboncer_main main_3 (.in_1(button_1_out), .Clk(button_1_out), .out_3(main_3_out_3));
  deboncer_main main_4 (.in_1(button_1_out), .Clk(button_1_out), .out_3(main_4_out_3));
  // deboncer_main main_5: pin names not known; wires that end beside it: button_1_out, button_1_out, main_5_p3
  deboncer_main main_6 (.in_1(button_1_out), .Clk(button_1_out), .out_3(main_6_out_3));
  deboncer_main main_7 (.in_1(button_1_out), .Clk(button_1_out), .out_3(main_7_out_3));
  deboncer_main main_8 (.in_1(button_1_out), .Clk(button_1_out), .out_3(main_8_out_3));
  deboncer_main main_9 (.in_1(button_1_out), .Clk(button_1_out), .out_3(main_9_out_3));
  // memorie_suma_main main_10: pin names not known; wires that end beside it: button_1_out, in_2, main_10_p3
  Multiplexer #(.width(4), .enable("false")) multiplexer_1 (
    .in1(bit_extender_1_out), .out(multiplexer_1_out));  // open: in0, sel
  Multiplexer #(.width(4), .enable("false")) multiplexer_2 (
    .in1(bit_extender_2_out), .out(multiplexer_2_out));  // open: in0, sel
  Multiplexer #(.width(4), .enable("false")) multiplexer_3 (
    .in1(bit_extender_3_out), .out(multiplexer_3_out));  // open: in0, sel
  Multiplexer #(.width(4), .enable("false")) multiplexer_4 (
    .in1(bit_extender_4_out), .out(multiplexer_4_out));  // open: in0, sel
  Clock clock_1 (.out(button_1_out));
  // incarcare_suma_predefinita_main main_11: pin names not known; wires that end beside it: main_6_out_3, main_7_out_3, main_8_out_3, main_9_out_3, main_11_p5, main_11_p6, main_11_p7, main_11_p8, main_11_p9
  dec_to_io_main main_12 (
    .Zecimal(main_10_p3), .N3(main_12_n3), .N2(main_12_n2), .N1(main_12_n1), .N0(main_12_n0));  // open: N4, N5
  // memorie_bancnote_main main_13: pin names not known; wires that end beside it: multiplexer_1_out, multiplexer_2_out, multiplexer_3_out, multiplexer_4_out, main_13_p5, main_13_p6, main_13_p7, main_13_p8
  // algoritm_retragere_main main_14: pin names not known; wires that end beside it: main_14_p1
  assign bit_extender_5_out = {{6{1'b0}}, main_13_p5};  // Bit_Extender bit_extender_5
  assign bit_extender_6_out = {{6{1'b0}}, main_13_p6};  // Bit_Extender bit_extender_6
  assign bit_extender_7_out = {{6{1'b0}}, main_13_p7};  // Bit_Extender bit_extender_7
  assign bit_extender_8_out = {{6{1'b0}}, main_13_p8};  // Bit_Extender bit_extender_8
  or or_1 (or_1_out, Afisare_Sold, main_11_p5);
  Multiplexer #(.width(4), .enable("false")) multiplexer_5 (
    .in0(main_11_p6), .in1(main_12_n0), .out(multiplexer_5_out), .sel(Afisare_Sold));
  Multiplexer #(.width(4), .enable("false")) multiplexer_6 (
    .in0(main_11_p7), .in1(main_12_n1), .out(multiplexer_6_out), .sel(Afisare_Sold));
  Multiplexer #(.width(4), .enable("false")) multiplexer_7 (
    .in0(main_11_p8), .in1(main_12_n2), .out(multiplexer_7_out), .sel(Afisare_Sold));
  Multiplexer #(.width(4), .enable("false")) multiplexer_8 (
    .in0(main_11_p9), .in1(main_12_n3), .out(multiplexer_8_out), .sel(Afisare_Sold));
  // memorie_suma_main main_15: pin names not known; wires that end beside it: main_15_p1
  // memorie_io_main main_16: pin names not known; wires that end beside it: main_1_out_3, main_2_out_3, main_3_out_3, or_1_out, button_1_out, multiplexer_5_out, multiplexer_6_out, multiplexer_7_out, multiplexer_8_out, main_4_out_3, main_5_p3, main_16_p12, out_3, out_4, out_5, out_6
  assign bit_extender_9_out = {{6{1'b0}}, out_3};  // Bit_Extender bit_extender_9
  Bit_Extender #(.in_width(14), .out_width(10)) bit_extender_10 (.in(main_15_p1), .out(main_14_p1));
  assign bit_extender_11_out = {{6{1'b0}}, out_4};  // Bit_Extender bit_extender_11
  assign bit_extender_12_out = {{6{1'b0}}, out_5};  // Bit_Extender bit_extender_12
  assign bit_extender_13_out = {{6{1'b0}}, out_6};  // Bit_Extender bit_extender_13
  // algoritm_depunere_main main_17: pin names not known; wires that end beside it: main_14_p1, bit_extender_13_out, bit_extender_5_out, bit_extender_12_out, bit_extender_6_out, bit_extender_11_out, bit_extender_7_out, bit_extender_9_out, bit_extender_8_out, main_17_p10, main_17_p11, main_17_p12, main_17_p13
endmodule
