// Logisim project io_to_dec.circ as structural Verilog: 1 circuit, main circuit main
module main (
  input  [3:0] N0,
  input  [3:0] N1,
  input  [3:0] N2,
  input  [3:0] N3,
  input  [3:0] N4,
  input  [3:0] N5,
  output [15:0] Zecimal
);

  wire [15:0] adder_1_out, adder_2_out, adder_3_out, bit_extender_1_out, bit_extender_2_out,
       bit_extender_3_out, bit_extender_4_out, bit_extender_5_out, multiplier_1_out, multiplier_2_out,
       multiplier_3_out, multiplier_4_out;

  assign bit_extender_1_out = {{12{1'b0}}, N0};  // Bit_Extender bit_extender_1
  assign bit_extender_2_out = {{12{1'b0}}, N1};  // Bit_Extender bit_extender_2
  assign bit_extender_3_out = {{12{1'b0}}, N2};  // Bit_Extender bit_extender_3
  assign bit_extender_4_out = {{12{1'b0}}, N3};  // Bit_Extender bit_extender_4
  assign bit_extender_5_out = {{12{1'b0}}, N4};  // Bit_Extender bit_extender_5
  Multiplier #(.width(16)) multiplier_1 (.a(bit_extender_2_out), .b(16'ha), .out(multiplier_1_out));  // open: cin, cout
  Multiplier #(.width(16)) multiplier_2 (
    .a(bit_extender_3_out), .b(16'h64), .out(multiplier_2_out));  // open: cin, cout
  Multiplier #(.width(16)) multiplier_3 (
    .a(bit_extender_4_out), .b(16'h3e8), .out(multiplier_3_out));  // open: cin, cout
  Multiplier #(.width(16)) multiplier_4 (
    .a(bit_extender_5_out), .b(16'h2710), .out(multiplier_4_out));  // open: cin, cout
  Adder #(.width(16)) adder_1 (.a(bit_extender_1_out), .b(multiplier_1_out), .out(adder_1_out));  // open: cin, cout
  Adder #(.width(16)) adder_2 (.a(adder_1_out), .b(multiplier_2_out), .out(adder_2_out));  // open: cin, cout
  Adder #(.width(16)) adder_3 (.a(adder_2_out), .b(multiplier_3_out), .out(adder_3_out));  // open: cin, cout
  Adder #(.width(16)) adder_4 (.a(adder_3_out), .b(multiplier_4_out), .out(Zecimal));  // open: cin, cout
endmodule
