// Logisim project mem_pin.circ as structural Verilog: 1 circuit, main circuit MEM-pin
module MEM_pin (
  input  [15:0] PIN_NOU,
  input  WE,
  input  [1:0] IN_ADR,
  input  CLK,
  input  CS,
  output [15:0] MEM_PIN
);

  wire not_1_out;

  assign MEM_PIN = WE ? PIN_NOU : 16'bz;  // Controlled_Buffer controlled_buffer_1
  not not_1 (not_1_out, WE);
  RAM #(.addrWidth(2), .dataWidth(16)) ram_1 (
    .addr(IN_ADR), .data(MEM_PIN), .sel(CS), .clk(CLK), .ld(not_1_out), .clr(1'b0));
endmodule
