// Logisim project memorie_bancnote.circ as structural Verilog: 1 circuit, main circuit main
module main (
  input  WE_BANCNOTE,
  input  Clock,
  input  [15:0] Up500,
  input  [15:0] Up200,
  input  [15:0] Up100,
  input  [15:0] Up50,
  input  [15:0] Up20,
  input  [15:0] Up10,
  output [15:0] Disp500,
  output [15:0] Disp200,
  output [15:0] Disp100,
  output [15:0] Disp50,
  output [15:0] Disp20,
  output [15:0] Disp10
);

  Register #(.width(16)) register_1 (.D(Up500), .en(WE_BANCNOTE), .Q(Disp500), .clk(Clock), .clr(1'b0));
  Register #(.width(16)) register_2 (.D(Up200), .en(WE_BANCNOTE), .Q(Disp200), .clk(Clock), .clr(1'b0));
  Register #(.width(16)) register_3 (.D(Up100), .en(WE_BANCNOTE), .Q(Disp100), .clk(Clock), .clr(1'b0));
  Register #(.width(16)) register_4 (.D(Up50), .en(WE_BANCNOTE), .Q(Disp50), .clk(Clock), .clr(1'b0));
  Register #(.width(16)) register_5 (.D(Up20), .en(WE_BANCNOTE), .Q(Disp20), .clk(Clock), .clr(1'b0));
  Register #(.width(16)) register_6 (.D(Up10), .en(WE_BANCNOTE), .Q(Disp10), .clk(Clock), .clr(1'b0));
endmodule
