// Logisim project memorie_io.circ as structural Verilog: 1 circuit, main circuit main
module main (
  input  Increment,
  input  Decrement,
  input  Confirm,
  input  Load,
  input  Clock,
  input  Clear,
  input  [3:0] Data0,
  input  [3:0] Data1,
  input  [3:0] Data2,
  input  [3:0] Data3,
  input  [3:0] Data4,
  input  [3:0] Data5,
  input  Next,
  input  Prev,
  output Validare,
  output [3:0] a0,
  output [3:0] a1,
  output [3:0] a2,
  output [3:0] a3,
  output [3:0] a4,
  output [3:0] a5,
  output [2:0] selected
);

  wire and_1_out, and_2_out, and_3_out, and_4_out, and_5_out, and_6_out, and_7_out, and_8_out, and_9_out,
       and_10_out, and_11_out, and_12_out, demultiplexer_1_out0, demultiplexer_1_out1, demultiplexer_1_out2,
       demultiplexer_1_out3, demultiplexer_1_out4, demultiplexer_1_out5, or_1_out, or_2_out, or_3_out,
       or_4_out, or_5_out, or_6_out, or_7_out, or_8_out, or_9_out, or_10_out, or_11_out, or_12_out, or_13_out;

  Demultiplexer #(.select(3), .enable("false")) demultiplexer_1 (
    .out0(demultiplexer_1_out0), .out1(demultiplexer_1_out1), .out2(demultiplexer_1_out2),
    .out3(demultiplexer_1_out3), .out4(demultiplexer_1_out4), .out5(demultiplexer_1_out5), .in(1'b1),
    .sel(selected));  // open: out6, out7
  and and_1 (and_1_out, demultiplexer_1_out0, Increment);
  and and_2 (and_2_out, demultiplexer_1_out0, Decrement);
  and and_3 (and_3_out, demultiplexer_1_out1, Increment);
  and and_4 (and_4_out, demultiplexer_1_out1, Decrement);
  and and_5 (and_5_out, demultiplexer_1_out2, Increment);
  and and_6 (and_6_out, demultiplexer_1_out2, Decrement);
  and and_7 (and_7_out, demultiplexer_1_out3, Increment);
  and and_8 (and_8_out, demultiplexer_1_out3, Decrement);
  and and_9 (and_9_out, demultiplexer_1_out4, Increment);
  and and_10 (and_10_out, demultiplexer_1_out4, Decrement);
  and and_11 (and_11_out, demultiplexer_1_out5, Increment);
  and and_12 (and_12_out, demultiplexer_1_out5, Decrement);
  or or_1 (or_1_out, Next, Prev);
  or or_2 (or_2_out, and_1_out, and_2_out);
  or or_3 (or_3_out, and_2_out, Load);
  or or_4 (or_4_out, and_3_out, and_4_out);
  or or_5 (or_5_out, and_4_out, Load);
  or or_6 (or_6_out, and_5_out, and_6_out);
  or or_7 (or_7_out, and_6_out, Load);
  or or_8 (or_8_out, and_7_out, and_8_out);
  or or_9 (or_9_out, and_8_out, Load);
  or or_10 (or_10_out, and_9_out, and_10_out);
  or or_11 (or_11_out, and_10_out, Load);
  or or_12 (or_12_out, and_11_out, and_12_out);
  or or_13 (or_13_out, and_12_out, Load);
  Counter #(.width(3), .max('h5)) counter_1 (
    .load(Prev), .count(or_1_out), .Q(selected), .clk(Clock), .clr(Clear));  // open: D, carry
  Counter #(.width(4), .max('hf)) counter_2 (
    .load(or_3_out), .D(Data0), .count(or_2_out), .Q(a0), .clk(Clock), .clr(Clear));  // open: carry
  Counter #(.width(4), .max('hf)) counter_3 (
    .load(or_5_out), .D(Data1), .count(or_4_out), .Q(a1), .clk(Clock), .clr(Clear));  // open: carry
  Counter #(.width(4), .max('hf)) counter_4 (
    .load(or_7_out), .D(Data2), .count(or_6_out), .Q(a2), .clk(Clock), .clr(Clear));  // open: carry
  Counter #(.width(4), .max('hf)) counter_5 (
    .load(or_9_out), .D(Data3), .count(or_8_out), .Q(a3), .clk(Clock), .clr(Clear));  // open: carry
  Counter #(.width(4), .max('hf)) counter_6 (
    .load(or_11_out), .D(Data4), .count(or_10_out), .Q(a4), .clk(Clock), .clr(Clear));  // open: carry
  Counter #(.width(4), .max('hf)) counter_7 (
    .load(or_13_out), .D(Data5), .count(or_12_out), .Q(a5), .clk(Clock), .clr(Clear));  // open: carry

  assign Validare = Confirm;

  // Notes on the sheet:
  //   reset
endmodule
