// Logisim project organigrama.circ as structural Verilog: 1 circuit, main circuit main
module main (
  input  VALIDARE,
  input  PIN_CORECT,
  input  IESIRE_CONT,
  input  OP_1,
  input  OP_0,
  input  RETRAGERE_POSIBILA,
  input  DEPUNERE_POSIBILA,
  input  CLK,
  input  RESET,
  output [4:0] STARE_CURENTA,
  output [4:0] STAREA_VIITOARE
);

  wire [5:5] multiplexer_1_out;

  D_Flip_Flop d_ff_1 (
    .clk(CLK), .D(STAREA_VIITOARE[4]), .Q(STARE_CURENTA[4]), .en(1'b1), .reset(RESET));  // open: Qn, preset
  D_Flip_Flop d_ff_2 (
    .clk(CLK), .D(STAREA_VIITOARE[3]), .Q(STARE_CURENTA[3]), .en(1'b1), .reset(RESET));  // open: Qn, preset
  D_Flip_Flop d_ff_3 (
    .clk(CLK), .D(STAREA_VIITOARE[2]), .Q(STARE_CURENTA[2]), .en(1'b1), .reset(RESET));  // open: Qn, preset
  Multiplexer #(.select(5)) multiplexer_1 (
    .in0(VALIDARE), .in1(PIN_CORECT), .in2(IESIRE_CONT), .in3(VALIDARE), .in4(OP_1), .in5(OP_0), .in6(OP_0),
    .in7(VALIDARE), .in8(1'b0), .in9(RETRAGERE_POSIBILA), .in10(1'b0), .in11(VALIDARE), .in12(VALIDARE),
    .in13(DEPUNERE_POSIBILA), .in14(1'b0), .in15(VALIDARE), .in16(VALIDARE), .in17(1'b0), .in18(VALIDARE),
    .in19(1'b0), .in20(1'b0), .in21(1'b0), .in22(1'b0), .in23(1'b0), .in24(1'b0), .in25(1'b0), .in26(1'b0),
    .in27(1'b0), .in28(1'b0), .in29(1'b0), .in30(1'b0), .in31(1'b0), .out(multiplexer_1_out[5]),
    .sel(STARE_CURENTA), .en(1'b1));
  D_Flip_Flop d_ff_4 (
    .clk(CLK), .D(STAREA_VIITOARE[1]), .Q(STARE_CURENTA[1]), .en(1'b1), .reset(RESET));  // open: Qn, preset
  D_Flip_Flop d_ff_5 (
    .clk(CLK), .D(STAREA_VIITOARE[0]), .Q(STARE_CURENTA[0]), .en(1'b1), .reset(RESET));  // open: Qn, preset
  ROM #(.addrWidth(6), .dataWidth(5)) rom_1 (
    .addr({multiplexer_1_out[5], STARE_CURENTA}), .data(STAREA_VIITOARE), .sel(1'b1));

  // Notes on the sheet:
  //   contents of rom_1 (hex, n*v repeats v):
  //   0 0 3 2 5 7 d 7 9 b c b c f 10 f 10 12 12 13*0 1 2 0 4 6 8 11 2 9 a c 2 2 e 10 2 2 12 2
endmodule
