// Logisim project test_schema_logica.circ as structural Verilog: 1 circuit, main circuit main
module main (
  input  [1:0] Adresa,
  input  Op_0,
  input  Op_1,
  output [3:0] out_4,
  output [3:0] out_5,
  output [3:0] out_6,
  output [3:0] out_7
);

  wire _10_out, _20_out, _50_out, _100_out, clock_1_out, Dec_out, Inc_out, main_1_out_3, main_2_out_3,
       main_3_out_3, main_4_out_3, main_5_out_3, main_6_out_3, main_7_out_3, main_8_p3, main_9_out_3,
       main_13_p7, main_13_p8, main_13_p9, main_13_p10, main_14_p1, main_14_p2, main_14_p6, main_14_p7,
       main_14_p10, main_15_p3, main_15_p4, main_15_p6, main_15_p7, main_15_p8, N_out, OK_out, or_1_out,
       or_2_out, P_out;
  wire [2:0] main_15_p2;
  wire [3:0] bit_extender_5_out, bit_extender_6_out, bit_extender_7_out, bit_extender_8_out, main_10_p6,
       main_10_p7, main_10_p8, main_10_p9, main_11_n0, main_11_n1, main_11_n2, main_11_n3, main_16_p17,
       multiplexer_6_out, multiplexer_7_out, multiplexer_8_out, multiplexer_9_out;
  wire [15:0] bit_extender_1_out, bit_extender_2_out, bit_extender_3_out, bit_extender_4_out,
       main_12_suma_out, main_17_p11, main_17_p12, main_17_p13, main_17_p14, main_17_p16, main_18_zecimal,
       main_20_p8, main_20_p9, main_20_p10, main_20_p11, main_20_p12, main_20_p13, main_20_p15, main_20_p16,
       main_20_p17, multiplexer_1_out, multiplexer_2_out, multiplexer_3_out, multiplexer_4_out,
       multiplexer_5_out;

  or or_1 (or_1_out, main_15_p2[1], main_15_p7);
  Multiplexer #(.width(16), .enable("false")) multiplexer_1 (
    .in0(main_17_p14), .in1(main_20_p10), .out(multiplexer_1_out), .sel(main_15_p2[1]));
  Clock clock_1 (.out(clock_1_out));
  Button _10 (.out(_10_out));
  Button _20 (.out(_20_out));
  Button _50 (.out(_50_out));
  Button _100 (.out(_100_out));
  Button Inc (.out(Inc_out));
  Button Dec (.out(Dec_out));
  Button N (.out(N_out));
  Button P (.out(P_out));
  Button OK (.out(OK_out));
  Multiplexer #(.width(16), .enable("false")) multiplexer_2 (
    .in0(main_17_p11), .in1(main_20_p9), .out(multiplexer_2_out), .sel(main_15_p2[1]));
  Multiplexer #(.width(16), .enable("false")) multiplexer_3 (
    .in0(main_17_p12), .in1(main_20_p12), .out(multiplexer_3_out), .sel(main_15_p2[1]));
  Multiplexer #(.width(16), .enable("false")) multiplexer_4 (
    .in0(main_17_p13), .in1(main_20_p15), .out(multiplexer_4_out), .sel(main_15_p2[1]));
  Multiplexer #(.width(16), .enable("false")) multiplexer_5 (
    .in0(main_17_p16), .in1(main_20_p17), .out(multiplexer_5_out), .sel(main_15_p2[1]));
  deboncer_main main_1 (.in_1(_10_out), .Clk(clock_1_out), .out_3(main_1_out_3));
  deboncer_main main_2 (.in_1(_20_out), .Clk(clock_1_out), .out_3(main_2_out_3));
  deboncer_main main_3 (.in_1(_50_out), .Clk(clock_1_out), .out_3(main_3_out_3));
  deboncer_main main_4 (.in_1(_100_out), .Clk(clock_1_out), .out_3(main_4_out_3));
  deboncer_main main_5 (.in_1(Inc_out), .Clk(clock_1_out), .out_3(main_5_out_3));
  deboncer_main main_6 (.in_1(Dec_out), .Clk(clock_1_out), .out_3(main_6_out_3));
  deboncer_main main_7 (.in_1(N_out), .Clk(clock_1_out), .out_3(main_7_out_3));
  // deboncer_main main_8: pin names not known; wires that end beside it: P_out, clock_1_out, main_8_p3
  deboncer_main main_9 (.in_1(OK_out), .Clk(clock_1_out), .out_3(main_9_out_3));
  // incarcare_suma_predefinita_main main_10: pin names not known; wires that end beside it: main_1_out_3, main_2_out_3, main_3_out_3, main_4_out_3, main_15_p2[2], main_10_p6, main_10_p7, main_10_p8, main_10_p9
  dec_to_io_main main_11 (
    .Zecimal(main_12_suma_out), .N3(main_11_n3), .N2(main_11_n2), .N1(main_11_n1), .N0(main_11_n0));  // open: N4, N5
  memorie_suma_main main_12 (
    .Adress(Adresa), .Suma_out(main_12_suma_out), .Data(multiplexer_1_out), .Wesuma(or_1_out),
    .Clock(clock_1_out));  // open: Clear
  // memorie_bancnote_main main_13: pin names not known; wires that end beside it: or_1_out, clock_1_out, multiplexer_2_out, multiplexer_3_out, multiplexer_4_out, multiplexer_5_out, main_13_p7, main_13_p8, main_13_p9, main_13_p10
  // organigrama2_main main_14: pin names not known; wires that end beside it: main_14_p1, main_14_p2, 1'b0, Op_1, Op_0, main_14_p6, main_14_p7, clock_1_out, 1'b0, main_14_p10
  Multiplexer #(.select(3), .width(4), .enable("false")) multiplexer_6 (
    .in1(main_11_n0), .in2(bit_extender_8_out), .in4(main_10_p6), .out(multiplexer_6_out), .sel(main_15_p2));  // open: in0, in3, in5, in6, in7
  Multiplexer #(.select(3), .width(4), .enable("false")) multiplexer_7 (
    .in1(main_11_n1), .in2(bit_extender_7_out), .in4(main_10_p7), .out(multiplexer_7_out), .sel(main_15_p2));  // open: in0, in3, in5, in6, in7
  Multiplexer #(.select(3), .width(4), .enable("false")) multiplexer_8 (
    .in1(main_11_n2), .in2(bit_extender_6_out), .in4(main_10_p8), .out(multiplexer_8_out), .sel(main_15_p2));  // open: in0, in3, in5, in6, in7
  Multiplexer #(.select(3), .width(4), .enable("false")) multiplexer_9 (
    .in1(main_11_n3), .in2(bit_extender_5_out), .in4(main_10_p9), .out(multiplexer_9_out), .sel(main_15_p2));  // open: in0, in3, in5, in6, in7
  assign bit_extender_1_out = {{12{1'b0}}, out_7};  // Bit_Extender bit_extender_1
  // iesiri_organigrama_main main_15: pin names not known; wires that end beside it: main_14_p10, main_15_p2[0], main_15_p3, main_15_p4, main_15_p2[1], main_15_p6, main_15_p7, main_15_p8
  assign bit_extender_2_out = {{12{1'b0}}, out_6};  // Bit_Extender bit_extender_2
  LED led_1 (.in(main_15_p3));
  assign bit_extender_3_out = {{12{1'b0}}, out_5};  // Bit_Extender bit_extender_3
  or or_2 (or_2_out, main_15_p2[2], main_15_p2[1], main_15_p2[0]);
  assign bit_extender_4_out = {{12{1'b0}}, out_4};  // Bit_Extender bit_extender_4
  // memorie_io_main main_16: pin names not known; wires that end beside it: main_5_out_3, main_6_out_3, main_9_out_3, or_2_out, clock_1_out, multiplexer_6_out, multiplexer_7_out, multiplexer_8_out, multiplexer_9_out, main_7_out_3, main_8_p3, main_14_p1, out_7, out_6, out_5, out_4, main_16_p17
  // algoritm_depunere_main main_17: pin names not known; wires that end beside it: main_12_suma_out, bit_extender_4_out, main_13_p7, bit_extender_3_out, main_13_p8, bit_extender_2_out, main_13_p9, bit_extender_1_out, main_13_p10, main_15_p8, main_17_p11, main_17_p12, main_17_p13, main_17_p14, main_14_p7, main_17_p16
  io_to_dec_main main_18 (.N0(out_7), .N1(out_6), .N2(out_5), .N3(out_4), .Zecimal(main_18_zecimal));  // open: N4, N5
  afisare_main main_19 (
    .a0(out_7), .a1(out_6), .a2(out_5), .a3(out_4), .a4(main_16_p17));  // open: Selected, d0, s0, d1, s1, d2, s2, d3, s3, d4, s4, a5, d5, s5
  // algoritm_retragere_main main_20: pin names not known; wires that end beside it: main_12_suma_out, main_18_zecimal, main_13_p7, main_13_p8, main_15_p4, main_13_p9, main_13_p10, main_20_p8, main_20_p9, main_20_p10, main_20_p11, main_20_p12, main_20_p13, main_14_p6, main_20_p15, main_20_p16, main_20_p17
  IDENTIFICATOR_CARD identificator_card_1 (
    .IN_PIN(main_18_zecimal), .PIN_NOU(main_18_zecimal), .VERIFY_WRITE_PIN(main_15_p6), .IN_ADR(Adresa),
    .PIN_CORECT(main_14_p2), .CLK(clock_1_out));
  Bit_Extender #(.in_width(16), .out_width(4)) bit_extender_5 (.in(main_20_p8), .out(bit_extender_5_out));
  Bit_Extender #(.in_width(16), .out_width(4)) bit_extender_6 (.in(main_20_p11), .out(bit_extender_6_out));
  Bit_Extender #(.in_width(16), .out_width(4)) bit_extender_7 (.in(main_20_p13), .out(bit_extender_7_out));
  Bit_Extender #(.in_width(16), .out_width(4)) bit_extender_8 (.in(main_20_p16), .out(bit_extender_8_out));
endmodule
